# Fritzing sketch pantalla_sensor (saved by Fritzing 0.9.3b)

parts:
  Componente1 = Arduino Uno (Rev3)
  U1 = GAS_SENSOR [package=mq-3]  # not connected
  LCD1 = LCD screen
  R1 = Resistor [tolerance=±5% resistance=1k package=THT]  # not connected
  VCC1 = Battery block 9V  # not connected
  Componente2 = MicroSD Card Module

nets:
  N1: Componente1.D10_PWM/SS, Componente2.CS
  N2: Componente1.D11_PWM/MOSI, Componente2.MOSI
  N3: Componente1.D12/MISO, Componente2.MISO
  N4: Componente1.D13/SCK, Componente2.SCK
  N5: Componente1.D2, LCD1.DB7
  N6: Componente1.D3_PWM, LCD1.DB6
  N7: Componente1.D4, LCD1.DB5
  N8: Componente1.D5_PWM, LCD1.DB4
  N9: Componente1.D6_PWM, LCD1.E
  N10: Componente1.D7, LCD1.RS
  N11: Componente1.5V, LCD1.LED+
  N12: Componente1.GND, LCD1.LED-

notes:
  AO
