# Fritzing sketch ParkingLayout (saved by Fritzing 0.9.3b)
stripboards: 1

parts:
  Part1 = Arduino Nano (Rev3.0) (ICSP)
  R1 = Resistor [tolerance=±5% resistance=220 package=THT]  # not connected
  J1 = Piezo Speaker

nets:
  N1: Part1.GND, J1.pin1
  N2: Part1.5V, J1.pin2

notes:
  SDA
  SCL
  GND
  VCC
  ToF laser sensor
  CAR, back light
  12V
  NANO
  BUZZER
