# Fritzing sketch scetch (saved by Fritzing 0.9.3b)

parts:
  Part1 = Arduino Nano (Rev3.0) (ICSP)
  R1 = Resistor [tolerance=±5% resistance=220 package="2010 [SMD]"]
  D1 = Diode [package=diode-hv]
  Q1 = NPN-Transistor [package="TO92 [THT]"]
  J1 = Basic Servo  # not connected
  S1 = Pushbutton [package="[SMD]"]
  R2 = Resistor [tolerance=±5% resistance=220 package="2010 [SMD]"]
  U1 = SWITCH_SPDT [package=kps-1290]
  VCC1 = Battery block 9V

nets:
  N1: Part1.GND, Q1.C
  N2: Part1.D4, R2.Pin_0
  N3: Part1.D5, R1.Pin_0
  N4: Part1.VIN, U1.O
  N5: Part1.5V, D1.C, S1.Pin_3, S1.Pin_4
  N6: R1.Pin_1, Q1.B
  N7: D1.A, Q1.E
  N8: U1.P, VCC1.+

notes:
  1N4001
  PN2222
  10K
  270
