# Fritzing sketch calaveraFritz (saved by Fritzing 0.9.3b)

parts:
  Componente1 = Arduino Nano (Rev3.0) (ICSP)
  VCC1 = Battery block 9V
  S1 = Taiway 100-SP-X-T1 SPDT Miniature Toggle Switch [part_number=100-SP-X-T1-0-0-B1-M2 package=THT]
  LED1 = LED - 3mm [color="Red (633nm)" package="3 mm [THT]"]
  hc-sr1 = hc-sr04
  J1 = Basic Servo

nets:
  N1: Componente1.D2, hc-sr1.Echo
  N2: Componente1.D3, hc-sr1.Trig
  N3: Componente1.VIN, S1.L1, LED1.cathode
  N4: Componente1.GND, VCC1.-
  VCC: Componente1.5V, hc-sr1.VCC, J1.vcc
  GND: hc-sr1.GND, J1.gnd
